// Logisim project PlayandPause.circ as structural Verilog: 1 circuit, main circuit Play_Pause
module Play_Pause (
);

  wire and_1_out, and_2_out, and_3_out, and_4_out, d_ff_1_q, d_ff_2_q, d_ff_3_q, d_ff_3_qn, j_k_ff_1_q,
       j_k_ff_1_qn, or_1_out, Pause1A_out, Pause1B_out, Play1A_out, Play1B_out, Reset1A_out, Reset1B_out;

  Button Play1A (.out(Play1A_out));
  Button Pause1A (.out(Pause1A_out));
  Button Play1B (.out(Play1B_out));
  Button Pause1B (.out(Pause1B_out));
  D_Flip_Flop d_ff_1 (.D(Play1A_out), .clk(Play1A_out), .Q(d_ff_1_q), .reset(Reset1A_out));  // open: Qn, preset
  and and_1 (and_1_out, d_ff_1_q, Pause1A_out);
  D_Flip_Flop d_ff_2 (.D(Play1B_out), .clk(Play1B_out), .Q(d_ff_2_q), .reset(Reset1B_out));  // open: Qn, preset
  and and_2 (and_2_out, d_ff_2_q, Pause1B_out);
  D_Flip_Flop d_ff_3 (
    .D(Play1A_out), .clk(Play1A_out), .Q(d_ff_3_q), .Qn(d_ff_3_qn), .reset(and_1_out));  // open: preset
  or or_1 (or_1_out, Play1B_out, and_2_out);
  J_K_Flip_Flop j_k_ff_1 (
    .J(or_1_out), .K(and_2_out), .clk(or_1_out), .Q(j_k_ff_1_q), .Qn(j_k_ff_1_qn), .reset(Reset1B_out));  // open: preset
  and and_3 (and_3_out, d_ff_3_qn, d_ff_1_q);
  Button Reset1A (.out(Reset1A_out));
  LED led_1 (.in(d_ff_3_q));
  LED led_2 (.in(and_3_out));
  and and_4 (and_4_out, j_k_ff_1_qn, d_ff_2_q);
  Button Reset1B (.out(Reset1B_out));
  LED led_3 (.in(j_k_ff_1_q));
  LED led_4 (.in(and_4_out));

  // Notes on the sheet:
  //   STAGE 1A - Play/Pause
  //   STAGE 1B - Play/Pause
  //   Play
  //   Pause
  //   Play
  //   Pause
endmodule
