// Logisim project main_cir.circ as structural Verilog: 1 circuit, main circuit Main_circuit
module Main_circuit (
  input  On_OFF
);

  wire and_1_out, and_2_out, and_3_out, and_4_out, and_5_out, and_6_out, and_7_out, and_8_out, and_9_out,
       and_10_out, and_11_out, and_12_out, and_13_out, and_14_out, and_15_out, and_16_out, and_17_out,
       and_18_out, and_19_out, and_20_out, and_21_out, and_22_out, and_23_out, and_24_out, and_25_out,
       and_26_out, and_27_out, and_28_out, and_29_out, and_30_out, and_31_out, and_32_out, and_33_out,
       and_34_out, and_35_out, and_36_out, and_37_out, and_38_out, and_39_out, and_40_out, and_41_out,
       and_42_out, and_43_out, and_44_out, and_45_out, and_46_out, and_47_out, and_48_out, and_49_out,
       and_50_out, and_51_out, and_52_out, and_53_out, and_54_out, and_55_out, and_56_out, and_57_out,
       and_58_out, and_59_out, and_60_out, and_61_out, and_62_out, and_63_out, and_64_out, and_65_out,
       and_66_out, and_67_out, and_68_out, and_69_out, and_70_out, and_71_out, and_72_out, and_73_out,
       and_74_out, and_75_out, and_76_out, and_77_out, and_78_out, and_79_out, and_80_out, and_83_out,
       buffer_1_out, buffer_2_out, buffer_3_out, buffer_4_out, buffer_5_out, buffer_6_out, button_1_out,
       button_2_out, d_ff_1_q, d_ff_2_q, d_ff_3_q, d_ff_4_q, d_ff_4_qn, d_ff_5_q, d_ff_6_q, d_ff_7_q,
       d_ff_8_q, d_ff_9_q, d_ff_10_q, d_ff_11_q, d_ff_12_q, d_ff_13_q, d_ff_14_q, d_ff_15_q, d_ff_16_q,
       d_ff_17_q, d_ff_18_q, d_ff_19_q, d_ff_20_q, DECREASE_out, GreaterThan9ThenChange_out,
       GreaterThan99Reset_out, If0ThenSet1_out, IfGreaterThan99Set1_out, INCREASE_out, j_k_ff_1_q,
       j_k_ff_1_qn, j_k_ff_2_qn, j_k_ff_3_qn, j_k_ff_4_q, j_k_ff_4_qn, j_k_ff_5_qn, j_k_ff_6_qn, j_k_ff_7_qn,
       j_k_ff_8_qn, j_k_ff_9_qn, j_k_ff_10_qn, j_k_ff_11_qn, j_k_ff_12_qn, j_k_ff_13_qn, j_k_ff_14_qn,
       LowerThan9NoChange_out, Next_Track_out, NoGreaterThan9_out, NoLowerThan0_out, nor_1_out, nor_2_out,
       nor_3_out, nor_4_out, not_1_out, not_2_out, not_3_out, not_4_out, not_5_out, not_6_out, not_7_out,
       not_8_out, not_9_out, not_10_out, not_11_out, not_12_out, not_13_out, not_14_out, not_15_out,
       not_16_out, not_17_out, not_18_out, not_19_out, not_20_out, not_21_out, not_22_out, not_23_out,
       not_24_out, not_25_out, not_26_out, not_27_out, not_28_out, not_29_out, not_30_out, not_31_out,
       not_32_out, not_33_out, not_34_out, not_35_out, not_36_out, not_37_out, not_38_out, not_39_out,
       not_40_out, not_41_out, not_42_out, not_43_out, not_44_out, not_45_out, or_1_out, or_2_out, or_3_out,
       or_4_out, or_5_out, or_6_out, or_7_out, or_8_out, or_9_out, or_10_out, or_11_out, or_12_out,
       or_13_out, or_14_out, or_15_out, or_16_out, or_17_out, or_18_out, or_19_out, or_20_out, or_21_out,
       or_22_out, or_23_out, or_24_out, or_25_out, or_26_out, or_27_out, or_28_out, or_29_out, or_30_out,
       or_31_out, or_32_out, or_33_out, or_34_out, or_35_out, or_36_out, or_37_out, or_38_out, or_39_out,
       or_40_out, or_41_out, or_42_out, or_43_out, or_44_out, or_45_out, or_46_out, or_47_out, or_48_out,
       or_49_out, or_50_out, or_51_out, or_52_out, or_53_out, Pause1A_out, Pause1B_out, Pause_out,
       Play1A_out, Play1B_out, Play_out, Pre_Track_out, Reset1A_out, Reset1B_out, Volume_Down_out,
       Volume_Up_out;
  wire [3:0] and_81_out, and_82_out, j_k_ff_2_q, j_k_ff_3_q, j_k_ff_7_q, j_k_ff_8_q;

  Button Play1A (.out(Play1A_out));
  Button Pause1A (.out(Pause1A_out));
  Button Play1B (.out(Play1B_out));
  Button Pause1B (.out(Pause1B_out));
  Button INCREASE (.out(INCREASE_out));
  Button DECREASE (.out(DECREASE_out));
  not not_1 (not_1_out, INCREASE_out);
  not not_2 (not_2_out, DECREASE_out);
  Button Play (.out(Play_out));
  Button Pause (.out(Pause_out));
  Button Volume_Up (.out(Volume_Up_out));
  Button Volume_Down (.out(Volume_Down_out));
  Button Next_Track (.out(Next_Track_out));
  Button Pre_Track (.out(Pre_Track_out));
  D_Flip_Flop d_ff_1 (.D(Play1A_out), .clk(Play1A_out), .Q(d_ff_1_q), .reset(Reset1A_out));  // open: Qn, preset
  and and_1 (and_1_out, d_ff_1_q, Pause1A_out);
  D_Flip_Flop d_ff_2 (.D(Play1B_out), .clk(Play1B_out), .Q(d_ff_2_q), .reset(Reset1B_out));  // open: Qn, preset
  and and_2 (and_2_out, d_ff_2_q, Pause1B_out);
  or or_1 (or_1_out, not_1_out, DECREASE_out);
  or or_2 (or_2_out, INCREASE_out, not_2_out);
  or or_3 (or_3_out, INCREASE_out, DECREASE_out);
  Button button_1 (.out(button_1_out));
  Button button_2 (.out(button_2_out));
  not not_3 (not_3_out, On_OFF);
  not not_4 (not_4_out, or_1_out);
  buf buffer_1 (buffer_1_out, or_3_out);
  buf buffer_2 (buffer_2_out, buffer_1_out);
  buf buffer_3 (buffer_3_out, buffer_2_out);
  D_Flip_Flop d_ff_3 (.D(Play_out), .clk(Play_out), .Q(d_ff_3_q), .reset(not_3_out));  // open: Qn, preset
  not not_5 (not_5_out, Volume_Up_out);
  not not_6 (not_6_out, Volume_Down_out);
  D_Flip_Flop d_ff_4 (
    .D(Play1A_out), .clk(Play1A_out), .Q(d_ff_4_q), .Qn(d_ff_4_qn), .reset(and_1_out));  // open: preset
  or or_4 (or_4_out, Play1B_out, and_2_out);
  and and_3 (and_3_out, not_4_out, or_2_out);
  and and_4 (and_4_out, or_1_out, d_ff_7_q);
  and and_5 (and_5_out, buffer_3_out, buffer_3_out);
  or or_5 (or_5_out, button_1_out, button_2_out);
  or or_6 (or_6_out, not_5_out, Volume_Down_out);
  not not_7 (not_7_out, or_6_out);
  or or_7 (or_7_out, Volume_Up_out, not_6_out);
  or or_8 (or_8_out, Volume_Up_out, Volume_Down_out);
  buf buffer_4 (buffer_4_out, or_8_out);
  buf buffer_5 (buffer_5_out, buffer_4_out);
  buf buffer_6 (buffer_6_out, buffer_5_out);
  D_Flip_Flop d_ff_5 (.D(or_9_out), .clk(and_5_out), .Q(d_ff_5_q));  // open: Qn, preset, reset
  or or_9 (or_9_out, and_3_out, and_4_out);
  nor nor_1 (nor_1_out, button_1_out, nor_2_out);
  nor nor_2 (nor_2_out, nor_1_out, button_2_out);
  not not_8 (not_8_out, LowerThan9NoChange_out);
  not not_9 (not_9_out, nor_2_out);
  and and_6 (and_6_out, d_ff_3_q, Pause_out);
  and and_7 (and_7_out, not_7_out, or_7_out);
  and and_8 (and_8_out, or_6_out, d_ff_8_q);
  J_K_Flip_Flop j_k_ff_1 (
    .J(or_4_out), .K(and_2_out), .clk(or_4_out), .Q(j_k_ff_1_q), .Qn(j_k_ff_1_qn), .reset(Reset1B_out));  // open: preset
  not not_10 (not_10_out, or_1_out);
  or or_10 (or_10_out, IfGreaterThan99Set1_out, If0ThenSet1_out);
  and and_9 (and_9_out, not_8_out, not_9_out);
  or or_11 (or_11_out, Play_out, and_6_out);
  or or_12 (or_12_out, and_7_out, and_8_out);
  and and_10 (and_10_out, buffer_6_out, buffer_6_out);
  and and_11 (and_11_out, d_ff_4_qn, d_ff_1_q);
  Button Reset1A (.out(Reset1A_out));
  and and_12 (and_12_out, not_10_out, d_ff_5_q);
  and and_13 (and_13_out, or_1_out, d_ff_9_q);
  J_K_Flip_Flop #(.trigger("falling")) j_k_ff_2 (
    .J(1'b1), .K(1'b1), .clk(or_5_out), .Q(j_k_ff_2_q[0]), .Qn(j_k_ff_2_qn), .preset(or_10_out),
    .reset(NoGreaterThan9_out));
  J_K_Flip_Flop #(.trigger("falling")) j_k_ff_3 (
    .J(1'b1), .K(1'b1), .clk(or_13_out), .Q(j_k_ff_3_q[0]), .Qn(j_k_ff_3_qn), .reset(IfGreaterThan99Set1_out));  // open: preset
  or or_13 (or_13_out, GreaterThan9ThenChange_out, and_9_out);
  J_K_Flip_Flop j_k_ff_4 (
    .J(or_11_out), .K(and_6_out), .clk(or_11_out), .Q(j_k_ff_4_q), .Qn(j_k_ff_4_qn), .reset(not_3_out));  // open: preset
  D_Flip_Flop d_ff_6 (.D(or_12_out), .clk(and_10_out), .Q(d_ff_6_q));  // open: Qn, preset, reset
  and and_14 (and_14_out, On_OFF, d_ff_6_q);
  LED led_1 (.in(d_ff_4_q));
  LED led_2 (.in(and_11_out));
  not not_11 (not_11_out, nor_2_out);
  not not_12 (not_12_out, nor_2_out);
  not not_13 (not_13_out, or_6_out);
  nor nor_3 (nor_3_out, Next_Track_out, nor_4_out);
  nor nor_4 (nor_4_out, nor_3_out, Pre_Track_out);
  or or_14 (or_14_out, Next_Track_out, Pre_Track_out);
  not not_14 (not_14_out, or_48_out);
  not not_15 (not_15_out, nor_4_out);
  and and_15 (and_15_out, j_k_ff_1_qn, d_ff_2_q);
  Button Reset1B (.out(Reset1B_out));
  D_Flip_Flop d_ff_7 (.D(or_15_out), .clk(and_5_out), .Q(d_ff_7_q));  // open: Qn, preset, reset
  or or_15 (or_15_out, and_12_out, and_13_out);
  and and_16 (and_16_out, nor_2_out, j_k_ff_2_q[0]);
  and and_17 (and_17_out, j_k_ff_2_qn, not_11_out);
  and and_18 (and_18_out, nor_2_out, j_k_ff_3_q[0]);
  and and_19 (and_19_out, j_k_ff_3_qn, not_12_out);
  and and_20 (and_20_out, not_13_out, d_ff_6_q);
  and and_21 (and_21_out, or_6_out, d_ff_10_q);
  or or_16 (or_16_out, and_64_out, and_73_out);
  and and_22 (and_22_out, not_14_out, not_15_out);
  LED led_3 (.in(j_k_ff_1_q));
  LED led_4 (.in(and_15_out));
  not not_16 (not_16_out, or_1_out);
  or or_17 (or_17_out, and_16_out, and_17_out);
  or or_18 (or_18_out, and_18_out, and_19_out);
  D_Flip_Flop d_ff_8 (.D(or_19_out), .clk(and_10_out), .Q(d_ff_8_q));  // open: Qn, preset, reset
  or or_19 (or_19_out, and_20_out, and_21_out);
  or or_20 (or_20_out, and_69_out, and_22_out);
  and and_23 (and_23_out, not_16_out, d_ff_7_q);
  and and_24 (and_24_out, or_1_out, d_ff_11_q);
  J_K_Flip_Flop #(.trigger("falling")) j_k_ff_5 (
    .J(or_17_out), .K(or_17_out), .clk(or_5_out), .Q(j_k_ff_2_q[1]), .Qn(j_k_ff_5_qn), .reset(or_21_out));  // open: preset
  or or_21 (or_21_out, NoLowerThan0_out, NoGreaterThan9_out);
  J_K_Flip_Flop #(.trigger("falling")) j_k_ff_6 (
    .J(or_18_out), .K(or_18_out), .clk(or_13_out), .Q(j_k_ff_3_q[1]), .Qn(j_k_ff_6_qn), .reset(or_22_out));  // open: preset
  or or_22 (or_22_out, GreaterThan99Reset_out, IfGreaterThan99Set1_out);
  not not_17 (not_17_out, or_6_out);
  and and_25 (and_25_out, On_OFF, d_ff_8_q);
  J_K_Flip_Flop #(.trigger("falling")) j_k_ff_7 (
    .J(On_OFF), .K(On_OFF), .clk(or_14_out), .Q(j_k_ff_7_q[0]), .Qn(j_k_ff_7_qn), .preset(or_16_out),
    .reset(and_63_out));
  not not_18 (not_18_out, nor_4_out);
  J_K_Flip_Flop #(.trigger("falling")) j_k_ff_8 (
    .J(On_OFF), .K(On_OFF), .clk(or_20_out), .Q(j_k_ff_8_q[0]), .Qn(j_k_ff_8_qn), .reset(and_64_out));  // open: preset
  not not_19 (not_19_out, nor_4_out);
  or or_23 (or_23_out, and_23_out, and_24_out);
  and and_26 (and_26_out, and_16_out, j_k_ff_2_q[1]);
  and and_27 (and_27_out, j_k_ff_5_qn, and_17_out);
  and and_28 (and_28_out, and_18_out, j_k_ff_3_q[1]);
  and and_29 (and_29_out, j_k_ff_6_qn, and_19_out);
  and and_30 (and_30_out, not_17_out, d_ff_8_q);
  and and_31 (and_31_out, or_6_out, d_ff_12_q);
  and and_32 (and_32_out, nor_4_out, j_k_ff_7_q[0]);
  and and_33 (and_33_out, j_k_ff_7_qn, not_18_out);
  and and_34 (and_34_out, nor_4_out, j_k_ff_8_q[0]);
  and and_35 (and_35_out, j_k_ff_8_qn, not_19_out);
  D_Flip_Flop d_ff_9 (.D(or_23_out), .clk(and_5_out), .Q(d_ff_9_q));  // open: Qn, preset, reset
  or or_24 (or_24_out, and_30_out, and_31_out);
  not not_20 (not_20_out, or_1_out);
  J_K_Flip_Flop #(.trigger("falling")) j_k_ff_9 (
    .J(or_25_out), .K(or_25_out), .clk(or_5_out), .Q(j_k_ff_2_q[2]), .Qn(j_k_ff_9_qn), .reset(or_26_out));  // open: preset
  or or_25 (or_25_out, and_26_out, and_27_out);
  or or_26 (or_26_out, NoLowerThan0_out, NoGreaterThan9_out);
  J_K_Flip_Flop #(.trigger("falling")) j_k_ff_10 (
    .J(or_27_out), .K(or_27_out), .clk(or_13_out), .Q(j_k_ff_3_q[2]), .Qn(j_k_ff_10_qn), .reset(or_28_out));  // open: preset
  or or_27 (or_27_out, and_28_out, and_29_out);
  or or_28 (or_28_out, GreaterThan99Reset_out, IfGreaterThan99Set1_out);
  D_Flip_Flop d_ff_10 (.D(or_24_out), .clk(and_10_out), .Q(d_ff_10_q));  // open: Qn, preset, reset
  J_K_Flip_Flop #(.trigger("falling")) j_k_ff_11 (
    .J(or_29_out), .K(or_29_out), .clk(or_14_out), .Q(j_k_ff_7_q[1]), .Qn(j_k_ff_11_qn), .reset(or_30_out));  // open: preset
  or or_29 (or_29_out, and_32_out, and_33_out);
  or or_30 (or_30_out, and_67_out, and_63_out);
  J_K_Flip_Flop #(.trigger("falling")) j_k_ff_12 (
    .J(or_31_out), .K(or_31_out), .clk(or_20_out), .Q(j_k_ff_8_q[1]), .Qn(j_k_ff_12_qn), .reset(or_32_out));  // open: preset
  or or_31 (or_31_out, and_34_out, and_35_out);
  or or_32 (or_32_out, and_68_out, and_64_out);
  and and_36 (and_36_out, not_20_out, d_ff_9_q);
  and and_37 (and_37_out, or_1_out, d_ff_13_q);
  not not_21 (not_21_out, or_6_out);
  and and_38 (and_38_out, On_OFF, d_ff_10_q);
  D_Flip_Flop d_ff_11 (.D(or_33_out), .clk(and_5_out), .Q(d_ff_11_q));  // open: Qn, preset, reset
  or or_33 (or_33_out, and_36_out, and_37_out);
  and and_39 (and_39_out, and_26_out, j_k_ff_2_q[2]);
  and and_40 (and_40_out, j_k_ff_9_qn, and_27_out);
  and and_41 (and_41_out, and_28_out, j_k_ff_3_q[2]);
  and and_42 (and_42_out, j_k_ff_10_qn, and_29_out);
  and and_43 (and_43_out, not_21_out, d_ff_10_q);
  and and_44 (and_44_out, or_6_out, d_ff_14_q);
  and and_45 (and_45_out, and_32_out, j_k_ff_7_q[1]);
  and and_46 (and_46_out, j_k_ff_11_qn, and_33_out);
  and and_47 (and_47_out, and_34_out, j_k_ff_8_q[1]);
  and and_48 (and_48_out, j_k_ff_12_qn, and_35_out);
  not not_22 (not_22_out, or_1_out);
  or or_34 (or_34_out, and_39_out, and_40_out);
  or or_35 (or_35_out, and_41_out, and_42_out);
  or or_36 (or_36_out, and_43_out, and_44_out);
  J_K_Flip_Flop #(.trigger("falling")) j_k_ff_13 (
    .J(or_37_out), .K(or_37_out), .clk(or_14_out), .Q(j_k_ff_7_q[2]), .Qn(j_k_ff_13_qn), .reset(or_39_out));  // open: preset
  or or_37 (or_37_out, and_45_out, and_46_out);
  J_K_Flip_Flop #(.trigger("falling")) j_k_ff_14 (
    .J(or_38_out), .K(or_38_out), .clk(or_20_out), .Q(j_k_ff_8_q[2]), .Qn(j_k_ff_14_qn), .reset(or_40_out));  // open: preset
  or or_38 (or_38_out, and_47_out, and_48_out);
  and and_49 (and_49_out, not_22_out, d_ff_11_q);
  and and_50 (and_50_out, or_1_out, d_ff_15_q);
  LedBar ledbar_1 (
    .led0(d_ff_5_q), .led1(d_ff_7_q), .led2(d_ff_9_q), .led3(d_ff_11_q), .led4(d_ff_13_q), .led5(d_ff_15_q),
    .led6(d_ff_17_q), .led7(d_ff_19_q));
  J_K_Flip_Flop #(.trigger("falling")) j_k_ff_15 (
    .J(or_34_out), .K(or_34_out), .clk(or_5_out), .Q(j_k_ff_2_q[3]), .preset(If0ThenSet1_out),
    .reset(NoGreaterThan9_out));  // open: Qn
  J_K_Flip_Flop #(.trigger("falling")) j_k_ff_16 (
    .J(or_35_out), .K(or_35_out), .clk(or_13_out), .Q(j_k_ff_3_q[3]), .reset(IfGreaterThan99Set1_out));  // open: Qn, preset
  and and_51 (and_51_out, On_OFF, j_k_ff_4_q);
  and and_52 (and_52_out, j_k_ff_4_qn, On_OFF);
  D_Flip_Flop d_ff_12 (.D(or_36_out), .clk(and_10_out), .Q(d_ff_12_q));  // open: Qn, preset, reset
  and and_53 (and_53_out, On_OFF, d_ff_12_q);
  or or_39 (or_39_out, and_67_out, and_63_out);
  or or_40 (or_40_out, and_68_out, and_64_out);
  and NoGreaterThan9 (NoGreaterThan9_out, j_k_ff_2_q[3], nor_2_out, j_k_ff_2_q[1]);
  and IfGreaterThan99Set1 (IfGreaterThan99Set1_out, j_k_ff_3_q[3], nor_2_out, j_k_ff_3_q[1]);
  LED led_5 (.in(and_51_out));
  LED led_6 (.in(and_52_out));
  not not_23 (not_23_out, or_6_out);
  and and_54 (and_54_out, and_45_out, j_k_ff_7_q[2]);
  and and_55 (and_55_out, j_k_ff_13_qn, and_46_out);
  and and_56 (and_56_out, and_47_out, j_k_ff_8_q[2]);
  and and_57 (and_57_out, j_k_ff_14_qn, and_48_out);
  D_Flip_Flop d_ff_13 (.D(or_41_out), .clk(and_5_out), .Q(d_ff_13_q));  // open: Qn, preset, reset
  or or_41 (or_41_out, and_49_out, and_50_out);
  and NoLowerThan0 (NoLowerThan0_out, j_k_ff_2_q[3], j_k_ff_2_q[1], j_k_ff_2_q[0]);
  or or_42 (or_42_out, j_k_ff_3_q[1], j_k_ff_3_q[2]);
  and GreaterThan99Reset (GreaterThan99Reset_out, j_k_ff_3_q[3], or_42_out, j_k_ff_3_q[0]);
  and and_58 (and_58_out, not_23_out, d_ff_12_q);
  and and_59 (and_59_out, or_6_out, d_ff_16_q);
  LedBar ledbar_2 (
    .led0(and_14_out), .led1(and_25_out), .led2(and_38_out), .led3(and_53_out), .led4(and_62_out),
    .led5(and_72_out), .led6(and_78_out), .led7(and_83_out));
  Hex_Digit_Display hex_digit_display_1 (.value(and_82_out));  // open: dp
  Hex_Digit_Display hex_digit_display_2 (.value(and_81_out));  // open: dp
  or or_43 (or_43_out, and_54_out, and_55_out);
  or or_44 (or_44_out, and_56_out, and_57_out);
  not not_24 (not_24_out, or_1_out);
  or LowerThan9NoChange (LowerThan9NoChange_out, j_k_ff_2_q[0], j_k_ff_2_q[1], j_k_ff_2_q[2], j_k_ff_2_q[3]);
  D_Flip_Flop d_ff_14 (.D(or_45_out), .clk(and_10_out), .Q(d_ff_14_q));  // open: Qn, preset, reset
  or or_45 (or_45_out, and_58_out, and_59_out);
  J_K_Flip_Flop #(.trigger("falling")) j_k_ff_17 (
    .J(or_43_out), .K(or_43_out), .clk(or_14_out), .Q(j_k_ff_7_q[3]), .preset(and_73_out), .reset(and_63_out));  // open: Qn
  J_K_Flip_Flop #(.trigger("falling")) j_k_ff_18 (
    .J(or_44_out), .K(or_44_out), .clk(or_20_out), .Q(j_k_ff_8_q[3]), .reset(and_64_out));  // open: Qn, preset
  and and_60 (and_60_out, not_24_out, d_ff_13_q);
  and and_61 (and_61_out, or_1_out, d_ff_17_q);
  and GreaterThan9ThenChange (GreaterThan9ThenChange_out, j_k_ff_2_q[0], nor_2_out, j_k_ff_2_q[3]);
  and and_62 (and_62_out, On_OFF, d_ff_14_q);
  and and_63 (and_63_out, j_k_ff_7_q[3], nor_4_out, j_k_ff_7_q[1]);
  and and_64 (and_64_out, j_k_ff_8_q[3], nor_4_out, j_k_ff_8_q[1]);
  or or_46 (or_46_out, and_60_out, and_61_out);
  not not_25 (not_25_out, j_k_ff_3_q[3]);
  not not_26 (not_26_out, j_k_ff_3_q[2]);
  not not_27 (not_27_out, j_k_ff_3_q[1]);
  not not_28 (not_28_out, j_k_ff_3_q[0]);
  not not_29 (not_29_out, or_6_out);
  and and_65 (and_65_out, not_29_out, d_ff_14_q);
  and and_66 (and_66_out, or_6_out, d_ff_18_q);
  and and_67 (and_67_out, j_k_ff_7_q[3], j_k_ff_7_q[1], j_k_ff_7_q[0]);
  or or_47 (or_47_out, j_k_ff_8_q[1], j_k_ff_8_q[2]);
  and and_68 (and_68_out, j_k_ff_8_q[3], or_47_out, j_k_ff_8_q[0]);
  D_Flip_Flop d_ff_15 (.D(or_46_out), .clk(and_5_out), .Q(d_ff_15_q));  // open: Qn, preset, reset
  not not_30 (not_30_out, j_k_ff_2_q[3]);
  not not_31 (not_31_out, j_k_ff_2_q[2]);
  not not_32 (not_32_out, j_k_ff_2_q[1]);
  not not_33 (not_33_out, j_k_ff_2_q[0]);
  or or_48 (or_48_out, j_k_ff_7_q[0], j_k_ff_7_q[1], j_k_ff_7_q[2], j_k_ff_7_q[3]);
  not not_34 (not_34_out, or_1_out);
  D_Flip_Flop d_ff_16 (.D(or_49_out), .clk(and_10_out), .Q(d_ff_16_q));  // open: Qn, preset, reset
  or or_49 (or_49_out, and_65_out, and_66_out);
  and and_69 (and_69_out, j_k_ff_7_q[0], nor_4_out, j_k_ff_7_q[3]);
  and and_70 (and_70_out, not_34_out, d_ff_15_q);
  and and_71 (and_71_out, or_1_out, d_ff_19_q);
  not not_35 (not_35_out, or_6_out);
  and and_72 (and_72_out, On_OFF, d_ff_16_q);
  and and_73 (and_73_out, not_43_out, not_42_out, not_41_out, not_40_out, not_39_out, not_38_out, not_37_out, not_36_out);
  or or_50 (or_50_out, and_70_out, and_71_out);
  and If0ThenSet1 (If0ThenSet1_out, not_33_out, not_32_out, not_31_out, not_30_out, not_28_out, not_27_out, not_26_out, not_25_out);
  and and_74 (and_74_out, not_35_out, d_ff_16_q);
  and and_75 (and_75_out, or_6_out, d_ff_20_q);
  not not_36 (not_36_out, j_k_ff_8_q[3]);
  not not_37 (not_37_out, j_k_ff_8_q[2]);
  not not_38 (not_38_out, j_k_ff_8_q[1]);
  not not_39 (not_39_out, j_k_ff_8_q[0]);
  D_Flip_Flop d_ff_17 (.D(or_50_out), .clk(and_5_out), .Q(d_ff_17_q));  // open: Qn, preset, reset
  or or_51 (or_51_out, and_74_out, and_75_out);
  not not_40 (not_40_out, j_k_ff_7_q[3]);
  not not_41 (not_41_out, j_k_ff_7_q[2]);
  not not_42 (not_42_out, j_k_ff_7_q[1]);
  not not_43 (not_43_out, j_k_ff_7_q[0]);
  not not_44 (not_44_out, or_1_out);
  Hex_Digit_Display hex_digit_display_3 (.value(j_k_ff_3_q));  // open: dp
  D_Flip_Flop d_ff_18 (.D(or_51_out), .clk(and_10_out), .Q(d_ff_18_q));  // open: Qn, preset, reset
  and and_76 (and_76_out, not_44_out, d_ff_17_q);
  and and_77 (and_77_out, or_1_out, or_2_out);
  Hex_Digit_Display hex_digit_display_4 (.value(j_k_ff_2_q));  // open: dp
  not not_45 (not_45_out, or_6_out);
  and and_78 (and_78_out, On_OFF, d_ff_18_q);
  D_Flip_Flop d_ff_19 (.D(or_52_out), .clk(and_5_out), .Q(d_ff_19_q));  // open: Qn, preset, reset
  or or_52 (or_52_out, and_76_out, and_77_out);
  and and_79 (and_79_out, not_45_out, d_ff_18_q);
  and and_80 (and_80_out, or_6_out, or_7_out);
  assign and_81_out = j_k_ff_7_q & {4{On_OFF}};  // AND_Gate and_81, 4 bits wide
  or or_53 (or_53_out, and_79_out, and_80_out);
  assign and_82_out = j_k_ff_8_q & {4{On_OFF}};  // AND_Gate and_82, 4 bits wide
  D_Flip_Flop d_ff_20 (.D(or_53_out), .clk(and_10_out), .Q(d_ff_20_q));  // open: Qn, preset, reset
  and and_83 (and_83_out, On_OFF, d_ff_20_q);

  // Notes on the sheet:
  //   STAGE 1A - Play/Pause
  //   STAGE 1B - Play/Pause
  //   Play
  //   Pause
  //   Play
  //   Pause
  //   STAGE 2 - Volume
  //   STAGE 3 - Track Counter
  //   Play
  //   Pause
  //   TRACK
  //   TRACK
endmodule
